# Fritzing sketch Untitled Sketch (saved by Fritzing 0.9.3b)
breadboards: 1

parts:
  Componente1 = Arduino Nano (Rev3.0)
  LED1 = RGB LED - (4 legs) [package="5 mm [THT]"]
  Componente2 = Arduino Uno (Rev3) - ICSP
  IC1 = DS3231MZ Real Time Clock
  sdCard1 = my_sdCard
  LCM1602_IIC2 = LCM1602 IIC [part_number="LCM1602 IIC" chip_label="LCM1602 IIC" package="DIP (Dual Inline) [THT]"]
  LCD2 = LCD screen
  S1 = Pushbutton [package="[THT]"]
  S2 = Pushbutton [package="[THT]"]
  R1 = Resistor [tolerance=±5% resistance=220 package=THT]
  R2 = Resistor [tolerance=±5% resistance=220 package=THT]
  R3 = Resistor [tolerance=±5% resistance=220 package=THT]
  S3 = Pushbutton [package="[THT]"]
  Componente3 = RFID-RC522-v2

nets:
  N1: Componente1.D1/TX, Componente2.D0/RX
  N2: Componente1.D0/RX, Componente2.D1/TX
  GND: Componente1.GND, IC1.Pin_1, LCM1602_IIC2.GND
  N3: Componente1.D3, S1.Pin_3, S1.Pin_4, R1.Pin_0
  N4: Componente1.D4, R3.Pin_0, S3.Pin_3, S3.Pin_4
  N5: Componente1.D5, S2.Pin_3, S2.Pin_4, R2.Pin_0
  N6: Componente1.D9, Componente3.RST
  N7: Componente1.D10, Componente3.SDA
  N8: Componente1.D11/MOSI, Componente3.MOSI
  N9: Componente1.D12/MISO, Componente3.MISO
  VIN: Componente1.VIN, IC1.Pin_2, LCM1602_IIC2.VCC
  N10: Componente1.A5, IC1.Pin_4, LCM1602_IIC2.SCL
  N11: Componente1.A4, IC1.Pin_3, LCM1602_IIC2.SDA
  3V3: Componente1.3V3, Componente3.3.3V
  N12: Componente1.D13/SCK, Componente3.SCK
  N13: LED1.red_cathode, Componente2.D5_PWM
  GND_2: LED1.common_anode, Componente2.GND, sdCard1.GND
  N14: LED1.green_cathode, Componente2.D6_PWM
  N15: LED1.blue_cathode, Componente2.D7
  N16: Componente2.A4/SDA, sdCard1.CS
  N17: Componente2.D11_PWM/MOSI, sdCard1.MOSI
  N18: Componente2.D12/MISO, sdCard1.MISO
  N19: Componente2.D13/SCK, sdCard1.SCK
  5V: Componente2.5V, sdCard1.VCC
  VSS: LCM1602_IIC2.VSS, LCD2.VSS
  VDD: LCM1602_IIC2.VDD, LCD2.VDD
  N20: LCM1602_IIC2.V0, LCD2.V0
  N21: LCM1602_IIC2.RS, LCD2.RS
  N22: LCM1602_IIC2.RW, LCD2.R/W
  N23: LCM1602_IIC2.E, LCD2.E
  N24: LCM1602_IIC2.D0, LCD2.DB0
  N25: LCM1602_IIC2.D1, LCD2.DB1
  N26: LCM1602_IIC2.D2, LCD2.DB2
  N27: LCM1602_IIC2.D3, LCD2.DB3
  N28: LCM1602_IIC2.D4, LCD2.DB4
  N29: LCM1602_IIC2.D5, LCD2.DB5
  N30: LCM1602_IIC2.D6, LCD2.DB6
  N31: LCM1602_IIC2.D7, LCD2.DB7
  N32: LCM1602_IIC2.A, LCD2.LED+
  N33: LCM1602_IIC2.K, LCD2.LED-
  N34: LCM1602_IIC2.LED_A, LCM1602_IIC2.LED_B
  N35: S1.Pin_1, S1.Pin_2, S2.Pin_1, S2.Pin_2, S3.Pin_1, S3.Pin_2
  N36: R1.Pin_1, R2.Pin_1, R3.Pin_1

custom parts:
  DS3231MZ Real Time Clock: DS3231MZ Real Time Clock. SO-8 surface mount version.
  my_sdCard: micro sdCard Adapter with 90º pin header. Use a filtering Capacitor between CS and GND if needed. PCB View Pinouts are Reversed for laying parallel on PCB using a 90º pin header.
  LCM1602 IIC: I2C-Module to use a 1602 or 2004 LCD on with the wire.h libory Serial LCD Modul
  RFID-RC522-v2: A simple China made RFID-RC522 Reader; do check the pin labels, as this is a MFRC522 based clone.
